// Logisim project minirv.circ as structural Verilog: 4 circuits, main circuit cpu
module cpu (
  input  rst,
  input  clk
);

  wire and_2_out, and_3_out, comparator_1_lt, comparator_2_eq, comparator_2_gt, decoder_1_out0,
       decoder_1_out1, decoder_1_out2, decoder_1_out3, decoder_2_out0, decoder_2_out1, minidecoder_1_is_add,
       minidecoder_1_is_addi, minidecoder_1_is_jalr, minidecoder_1_is_lbu, minidecoder_1_is_lui,
       minidecoder_1_is_lw, minidecoder_1_is_sb, minidecoder_1_is_sw, or_1_out, or_2_out, or_3_out, or_4_out,
       or_5_out, or_6_out, or_7_out, or_8_out, priority_encoder_2_p2, rgb_video_1_p3;
  wire [1:0] bitselector_1_out, bitselector_2_out;
  wire [2:0] priority_encoder_1_p5;
  wire [4:0] bit_extender_4_out, minidecoder_1_rd, minidecoder_1_rs1, minidecoder_1_rs2, shifter_4_out;
  wire [7:0] bitselector_3_out, bitselector_4_out, bitselector_5_out, rgb_video_1_p5;
  wire [23:0] bit_extender_1_out, bit_extender_2_out, bit_extender_6_out, shifter_1_out, shifter_2_out;
  wire [31:0] adder_1_out, adder_2_out, adder_3_out, and_1_out, bit_extender_3_out, bit_extender_5_out,
       minidecoder_1_imm, minigpr_1_rdata1, minigpr_1_rdata2, multiplexer_1_out, multiplexer_2_out,
       multiplexer_3_out, multiplexer_4_out, ram_1_dout, register_1_q, rom_1_data, shifter_3_out,
       shifter_5_out, shifter_6_out, subtractor_1_out;

  Register #(.width(32)) register_1 (.D(multiplexer_1_out), .clk(clk), .Q(register_1_q), .clr(rst));  // open: en
  Bit_Extender #(.in_width(32), .out_width(24), .\type ("zero")) bit_extender_1 (
    .in(register_1_q), .out(bit_extender_1_out));
  Shifter #(.shift("lr"), .width(24)) shifter_1 (.in(bit_extender_1_out), .\dist (5'b00010), .out(shifter_1_out));
  ROM #(.addrWidth(24), .dataWidth(32)) rom_1 (.addr(shifter_1_out), .data(rom_1_data));
  Multiplexer #(.width(32)) multiplexer_1 (
    .in0(adder_1_out), .in1(and_1_out), .out(multiplexer_1_out), .sel(minidecoder_1_is_jalr));
  Adder #(.width(32)) adder_1 (.a(register_1_q), .b(32'h4), .out(adder_1_out));  // open: cin, cout
  assign and_1_out = adder_3_out & 32'hfffffffe;  // AND_Gate and_1, 32 bits wide
  miniDecoder minidecoder_1 (
    .inst(rom_1_data), .rd(minidecoder_1_rd), .rs1(minidecoder_1_rs1), .rs2(minidecoder_1_rs2),
    .is_addi(minidecoder_1_is_addi), .is_jalr(minidecoder_1_is_jalr), .is_add(minidecoder_1_is_add),
    .is_lui(minidecoder_1_is_lui), .is_lw(minidecoder_1_is_lw), .is_lbu(minidecoder_1_is_lbu),
    .is_sb(minidecoder_1_is_sb), .is_sw(minidecoder_1_is_sw), .imm(minidecoder_1_imm));
  // Priority_Encoder priority_encoder_1: pin names not known; wires that end beside it: minidecoder_1_is_addi, minidecoder_1_is_jalr, minidecoder_1_is_add, minidecoder_1_is_lui, priority_encoder_1_p5, minidecoder_1_is_lw, minidecoder_1_is_lbu, minidecoder_1_is_sb, minidecoder_1_is_sw
  Multiplexer #(.select(3), .width(32)) multiplexer_2 (
    .in0(adder_3_out), .in1(adder_1_out), .in2(adder_2_out), .in3(minidecoder_1_imm),
    .in4(multiplexer_3_out), .in5(multiplexer_3_out), .out(multiplexer_2_out), .sel(priority_encoder_1_p5));  // open: in6, in7
  or or_1 (or_1_out, minidecoder_1_is_addi, minidecoder_1_is_jalr, minidecoder_1_is_lui, minidecoder_1_is_lw, minidecoder_1_is_lbu, minidecoder_1_is_add);
  miniGPR minigpr_1 (
    .radd1(minidecoder_1_rs1), .radd2(minidecoder_1_rs2), .rst(rst), .clk(clk), .wdata(multiplexer_2_out),
    .waddr(minidecoder_1_rd), .we(or_1_out), .rdata1(minigpr_1_rdata1), .rdata2(minigpr_1_rdata2));
  Adder #(.width(32)) adder_2 (.a(minigpr_1_rdata1), .b(minigpr_1_rdata2), .out(adder_2_out));  // open: cin, cout
  Adder #(.width(32)) adder_3 (.a(minigpr_1_rdata1), .b(minidecoder_1_imm), .out(adder_3_out));  // open: cin, cout
  // Priority_Encoder #(.select(1)) priority_encoder_2: pin names not known; wires that end beside it: minidecoder_1_is_lbu, priority_encoder_2_p2, minidecoder_1_is_lw
  Multiplexer #(.width(32)) multiplexer_3 (
    .in0(bit_extender_3_out), .in1(ram_1_dout), .out(multiplexer_3_out), .sel(priority_encoder_2_p2));
  Decoder #(.select(2)) decoder_1 (
    .out0(decoder_1_out0), .out1(decoder_1_out1), .out2(decoder_1_out2), .out3(decoder_1_out3),
    .sel(bitselector_1_out));  // open: en
  Bit_Extender #(.in_width(32), .out_width(24), .\type ("zero")) bit_extender_2 (
    .in(adder_3_out), .out(bit_extender_2_out));
  BitSelector #(.group(2), .width(32)) bitselector_1 (.in(adder_3_out), .out(bitselector_1_out), .sel(4'b0000));
  Shifter #(.shift("lr"), .width(24)) shifter_2 (.in(bit_extender_2_out), .\dist (5'b00010), .out(shifter_2_out));
  assign bit_extender_3_out = {{24{1'b0}}, bitselector_3_out};  // Bit_Extender bit_extender_3
  or or_2 (or_2_out, minidecoder_1_is_lw, minidecoder_1_is_lbu);
  BitSelector #(.group(2), .width(32)) bitselector_2 (.in(adder_3_out), .out(bitselector_2_out), .sel(4'b0000));
  BitSelector #(.group(8), .width(32)) bitselector_3 (
    .in(ram_1_dout), .out(bitselector_3_out), .sel(bitselector_2_out));
  or or_3 (or_3_out, decoder_1_out3, minidecoder_1_is_sw);
  or or_4 (or_4_out, minidecoder_1_is_sb, minidecoder_1_is_sw);
  or or_5 (or_5_out, decoder_1_out2, minidecoder_1_is_sw);
  or or_6 (or_6_out, decoder_1_out0, minidecoder_1_is_sw);
  or or_7 (or_7_out, decoder_1_out1, minidecoder_1_is_sw);
  and and_2 (and_2_out, or_4_out, decoder_2_out0);
  RAM #(.addrWidth(24), .asyncread("true"), .byteenables("byteEnables"), .dataWidth(32), .\type ("nonvolatile")) ram_1 (
    .addr(shifter_2_out), .we(and_2_out), .oe(or_2_out), .clk(clk), .din(multiplexer_4_out),
    .dout(ram_1_dout), .be3(or_3_out), .be2(or_5_out), .be1(or_7_out), .be0(or_6_out));
  Subtractor #(.width(32)) subtractor_1 (.a(adder_3_out), .b(32'h20000000), .out(subtractor_1_out));  // open: bin, bout
  Comparator #(.width(32)) comparator_1 (.a(adder_3_out), .b(32'h20040000), .lt(comparator_1_lt));  // open: gt, eq
  Comparator #(.width(32)) comparator_2 (
    .a(adder_3_out), .b(32'h20000000), .gt(comparator_2_gt), .eq(comparator_2_eq));  // open: lt
  assign bit_extender_4_out = {{3{1'b0}}, bitselector_1_out};  // Bit_Extender bit_extender_4
  BitSelector #(.group(8), .width(32)) bitselector_4 (.in(minigpr_1_rdata2), .out(bitselector_4_out), .sel(2'b00));
  Shifter #(.shift("lr"), .width(32)) shifter_3 (.in(subtractor_1_out), .\dist (5'b00010), .out(shifter_3_out));
  assign bit_extender_5_out = {{24{1'b0}}, bitselector_4_out};  // Bit_Extender bit_extender_5
  Shifter #(.width(5)) shifter_4 (.in(bit_extender_4_out), .\dist (3'b011), .out(shifter_4_out));
  or or_8 (or_8_out, comparator_2_gt, comparator_2_eq);
  Shifter #(.width(32)) shifter_5 (.in(bit_extender_5_out), .\dist (shifter_4_out), .out(shifter_5_out));
  Multiplexer #(.width(32)) multiplexer_4 (
    .in0(shifter_5_out), .in1(minigpr_1_rdata2), .out(multiplexer_4_out), .sel(minidecoder_1_is_sw));
  BitSelector #(.group(8), .width(32)) bitselector_5 (.in(shifter_3_out), .out(bitselector_5_out), .sel(2'b00));
  and and_3 (and_3_out, comparator_1_lt, or_8_out);
  Decoder decoder_2 (.out0(decoder_2_out0), .out1(decoder_2_out1), .sel(and_3_out));  // open: en
  Bit_Extender #(.in_width(32), .out_width(24), .\type ("zero")) bit_extender_6 (
    .in(minigpr_1_rdata2), .out(bit_extender_6_out));
  // RGB_Video #(.cursor("No Cursor"), .height(256), .width(256)) rgb_video_1: pin names not known; wires that end beside it: rst, clk, rgb_video_1_p3, bitselector_5_out, rgb_video_1_p5, bit_extender_6_out
  Shifter #(.shift("lr"), .width(32)) shifter_6 (.in(shifter_3_out), .\dist (5'b01000), .out(shifter_6_out));
  Bit_Extender #(.in_width(32), .out_width(8)) bit_extender_7 (.in(shifter_6_out), .out(rgb_video_1_p5));
  and and_4 (rgb_video_1_p3, minidecoder_1_is_sw, decoder_2_out1);

  // Notes on the sheet:
  //   contents of rom_1 (hex, n*v repeats v):
  //   413 93137 10113 10b7 dbc08093 80e7 fe012823 fea10923 fea12423 fe914203 fe4109a3 ff012783 f787b3
  //   f787b3 4b6b7 af868693 fdc10113 d787b3 10000713 f12423 10593 100793 b00513 2112023 12023 12223 e12623
  //   e12823 f10a23 10b7 a8408093 80e7 2012083 2410113 8067 ff410113 112423 10b7 a7c08093 80e7 513 1800093
  //   80e7 812083 513 c10113 8067 852583 feb12823 fe812e23 3437 80840413 ff014183 3401b3 1c183 ff114203
  //   440233 24203 4181b3 ff214203 440233 24203 4181b3 ff314203 440233 24203 4181b3 3237 80020213 320233
  //   24203 ffc12403 420233 420233 410233 11b7 86418193 fe312823 14800193 fe312623 fec22203 20067 1052703
  //   52683 452783 fe810113 e12423 112a23 812823 912623 fed12823 fef12623 13737 a0070713 fe012223 ff314203
  //   fe4102a3 fef14203 fe410223 fe412203 470233 24203 fe4105a3 ff214203 fe4102a3 fee14203 fe410223
  //   fe412203 470233 24203 fe410523 ff114203 fe4102a3 fed14203 fe410223 fe412203 470233 24203 fe4104a3
  //   ff014203 fe4102a3 fec14203 fe410223 fe412203 470233 24203 fe410423 fe812703 c52603 fee12823 fe812e23
  //   3437 80840413 ff014183 3401b3 1c183 ff114203 440233 24203 4181b3 ff214203 440233 24203 4181b3
  //   ff314203 440233 24203 4181b3 3237 80020213 320233 24203 ffc12403 420233 420233 410233 66800193
  //   fe312823 28800193 fe312623 fec22203 20067 c68733 10000513 fe812e23 fe912c23 fee12823 50413 ff012483
  //   fe812423 feb14183 3181b3 fe312423 fe914183 3181b3 fe912423 feb14203 420233 fe412423 fe914203 4181b3
  //   3181b3 fe312a23 fe912423 33237 90020213 feb14183 4181b3 1c183 fe3103a3 fea14183 4181b3 1c183
  //   fe310323 fe914183 4181b3 1c183 fe3102a3 fe814183 4181b3 1c183 fe310223 ff412183 fe412203 440233
  //   120213 fe412423 feb14203 420233 fe412423 fe914203 4181b3 3237 90820213 320233 ff812483 ffc12403
  //   24203 420233 420233 410233 11b7 86818193 fe312823 39000193 fe312623 fec22203 20067 812703 10000513
  //   e78733 fe812e23 fe912c23 fee12823 50413 ff012483 fe812423 feb14183 3181b3 fe312423 fe914183 3181b3
  //   fe912423 feb14203 420233 fe412423 fe914203 4181b3 3181b3 fe312a23 fe912423 33237 90020213 feb14183
  //   4181b3 1c183 fe3103a3 fea14183 4181b3 1c183 fe310323 fe914183 4181b3 1c183 fe3102a3 fe814183 4181b3
  //   1c183 fe310223 ff412183 fe412203 440233 120213 fe412423 feb14203 420233 fe412423 fe914203 4181b3
  //   3237 90820213 320233 ff812483 ffc12403 24203 420233 420233 410233 11b7 86818193 fe312823 49c00193
  //   fe312623 fec22203 20067 8*f787b3 d787b3 f787b3 f787b3 20000437 f40433 812783 c60633 c60633 fef12423
  //   feb14183 3181b3 fe312423 fe914183 fff78213 fe412423 feb14203 420233 fe412423 fe914203 4181b3 3237
  //   91820213 418233 24203 420233 420233 410233 65400193 fe312823 54000193 fe312623 fec22203 20067 493
  //   40513 b12223 c12023 10b7 de008093 80e7 12603 412583 812783 148493 40040413 c585b3 fef12823 fe912623
  //   fe812e23 fe912c23 2437 70040413 ff014183 340233 100193 320023 fec14183 3401b3 18023 24183 ff114483
  //   940233 100493 920023 fed14483 9404b3 48023 24483 9181b3 ff214483 940233 100493 920023 fee14483
  //   9404b3 48023 24483 9181b3 ff314483 940233 100493 920023 fef14483 9404b3 48023 24483 9181b3 3237
  //   80020213 320233 24203 ff812483 ffc12403 420233 420233 410233 65400193 fe312823 54400193 fe312623
  //   fec22203 20067 1412083 1012403 c12483 1810113 8067 10000713 fec12823 fee12623 fe812e23 fe912c23 2437
  //   70040413 ff014183 340233 100193 320023 fec14183 3401b3 18023 24183 ff114483 940233 100493 920023
  //   fed14483 9404b3 48023 24483 9181b3 ff214483 940233 100493 920023 fee14483 9404b3 48023 24483 9181b3
  //   ff314483 940233 100493 920023 fef14483 9404b3 48023 24483 9181b3 3237 80020213 320233 24203 ff812483
  //   ffc12403 420233 420233 410233 74c00193 fe312823 28800193 fe312623 fec22203 20067 812703 fee12823
  //   fec12623 fe812e23 fe912c23 2437 70040413 ff014183 340233 100193 320023 fec14183 3401b3 18023 24183
  //   ff114483 940233 100493 920023 fed14483 9404b3 48023 24483 9181b3 ff214483 940233 100493 920023
  //   fee14483 9404b3 48023 24483 9181b3 ff314483 940233 100493 920023 fef14483 9404b3 48023 24483 9181b3
  //   3237 80020213 320233 24203 ff812483 ffc12403 420233 420233 410233 11b7 83418193 fe312823 39000193
  //   fe312623 fec22203 20067 1012403 1412083 c12483 40637 20000537 1810113 1237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
endmodule

module miniDecoder (
  input  [31:0] inst,
  output [4:0] rd,
  output [4:0] rs1,
  output [4:0] rs2,
  output is_addi,
  output is_jalr,
  output is_add,
  output is_lui,
  output is_lw,
  output is_lbu,
  output is_sb,
  output is_sw,
  output [31:0] imm
);

  wire comparator_1_eq, comparator_2_eq, comparator_3_eq, comparator_4_eq, comparator_5_eq, comparator_6_eq,
       comparator_7_eq, comparator_9_eq, comparator_10_eq, comparator_11_eq, comparator_12_eq,
       comparator_13_eq, comparator_14_eq, comparator_15_eq, comparator_16_eq, is_i_type_out, is_s_type_out;
  wire [1:0] priority_encoder_1_out;
  wire [31:0] bit_extender_1_out, bit_extender_2_out, bit_extender_3_out, shifter_1_out;

  Comparator #(.width(3)) comparator_1 (.a(inst[14:12]), .b(3'b000), .eq(comparator_1_eq));  // open: gt, lt
  Comparator #(.width(7)) comparator_2 (.a(inst[6:0]), .b(7'b0010011), .eq(comparator_2_eq));  // open: gt, lt
  and and_1 (is_addi, comparator_1_eq, comparator_2_eq);
  Comparator #(.width(3)) comparator_3 (.a(inst[14:12]), .b(3'b000), .eq(comparator_3_eq));  // open: gt, lt
  Comparator #(.width(7)) comparator_4 (.a(inst[6:0]), .b(7'b1100111), .eq(comparator_4_eq));  // open: gt, lt
  and and_2 (is_jalr, comparator_3_eq, comparator_4_eq);
  Comparator #(.width(3)) comparator_5 (.a(inst[14:12]), .b(3'b000), .eq(comparator_5_eq));  // open: gt, lt
  Comparator #(.width(7)) comparator_6 (.a(inst[6:0]), .b(7'b0110011), .eq(comparator_6_eq));  // open: gt, lt
  and and_3 (is_add, comparator_5_eq, comparator_7_eq, comparator_6_eq);
  Comparator #(.width(7)) comparator_7 (.a(inst[31:25]), .b({7{1'b0}}), .eq(comparator_7_eq));  // open: gt, lt
  Comparator #(.width(7)) comparator_8 (.a(inst[6:0]), .b(7'b0110111), .eq(is_lui));  // open: gt, lt
  Comparator #(.width(3)) comparator_9 (.a(inst[14:12]), .b(3'b010), .eq(comparator_9_eq));  // open: gt, lt
  Comparator #(.width(7)) comparator_10 (.a(inst[6:0]), .b(7'b0000011), .eq(comparator_10_eq));  // open: gt, lt
  and and_4 (is_lw, comparator_9_eq, comparator_10_eq);
  Comparator #(.width(3)) comparator_11 (.a(inst[14:12]), .b(3'b100), .eq(comparator_11_eq));  // open: gt, lt
  Comparator #(.width(7)) comparator_12 (.a(inst[6:0]), .b(7'b0000011), .eq(comparator_12_eq));  // open: gt, lt
  and and_5 (is_lbu, comparator_11_eq, comparator_12_eq);
  Comparator #(.width(3)) comparator_13 (.a(inst[14:12]), .b(3'b000), .eq(comparator_13_eq));  // open: gt, lt
  Comparator #(.width(7)) comparator_14 (.a(inst[6:0]), .b(7'b0100011), .eq(comparator_14_eq));  // open: gt, lt
  and and_6 (is_sb, comparator_13_eq, comparator_14_eq);
  Comparator #(.width(3)) comparator_15 (.a(inst[14:12]), .b(3'b010), .eq(comparator_15_eq));  // open: gt, lt
  Comparator #(.width(7)) comparator_16 (.a(inst[6:0]), .b(7'b0100011), .eq(comparator_16_eq));  // open: gt, lt
  and and_7 (is_sw, comparator_15_eq, comparator_16_eq);
  or is_s_type (is_s_type_out, is_sw, is_sb);
  or is_i_type (is_i_type_out, is_addi, is_lw, is_lbu, is_jalr);
  assign bit_extender_1_out = {{20{inst[31]}}, inst[31:20]};  // Bit_Extender bit_extender_1
  assign bit_extender_2_out = {{20{inst[31]}}, {inst[31:25], inst[11:7]}};  // Bit_Extender bit_extender_2
  Priority_Encoder #(.select(2)) priority_encoder_1 (
    .in0(is_s_type_out), .in1(is_i_type_out), .in2(is_lui), .in3(is_add), .out(priority_encoder_1_out));  // open: gs, en_out, en_in
  assign bit_extender_3_out = {{12{1'b0}}, inst[31:12]};  // Bit_Extender bit_extender_3
  Shifter #(.width(32)) shifter_1 (.in(bit_extender_3_out), .\dist (5'b01100), .out(shifter_1_out));
  Multiplexer #(.select(2), .width(32)) multiplexer_1 (
    .in0(bit_extender_2_out), .in1(bit_extender_1_out), .in2(shifter_1_out), .in3({32{1'b0}}), .out(imm),
    .sel(priority_encoder_1_out));

  assign rd = inst[11:7];
  assign rs1 = inst[19:15];
  assign rs2 = inst[24:20];
endmodule

module miniGPR (
  input  [4:0] radd1,
  input  [4:0] radd2,
  input  rst,
  input  clk,
  input  [31:0] wdata,
  input  [4:0] waddr,
  input  we,
  output [31:0] rdata1,
  output [31:0] rdata2
);

  wire decoder_1_out0, decoder_1_out1, decoder_1_out2, decoder_1_out3, decoder_1_out4, decoder_1_out5,
       decoder_1_out6, decoder_1_out7, decoder_1_out8, decoder_1_out9, decoder_1_out10, decoder_1_out11,
       decoder_1_out12, decoder_1_out13, decoder_1_out14, decoder_1_out15;
  wire [31:0] x0_zero_q, x1_ra_q, x2_sp_q, x3_gp_q, x4_tp_q, x5_t0_q, x6_t1_q, x7_t2_q, x8_fp_q, x9_s1_q,
       x10_a0_q, x11_a1_q, x12_a2_q, x13_a3_q, x14_a4_q, x15_a5_q;

  Decoder #(.select(5)) decoder_1 (
    .out0(decoder_1_out0), .out1(decoder_1_out1), .out2(decoder_1_out2), .out3(decoder_1_out3),
    .out4(decoder_1_out4), .out5(decoder_1_out5), .out6(decoder_1_out6), .out7(decoder_1_out7),
    .out8(decoder_1_out8), .out9(decoder_1_out9), .out10(decoder_1_out10), .out11(decoder_1_out11),
    .out12(decoder_1_out12), .out13(decoder_1_out13), .out14(decoder_1_out14), .out15(decoder_1_out15),
    .sel(waddr), .en(we));  // open: out16, out17, out18, out19, out20, out21, out22, out23, out24, out25, out26, out27, out28, out29, out30, out31
  Register #(.width(32)) x0_zero (.D(wdata), .en(1'b0), .clk(clk), .Q(x0_zero_q), .clr(rst));
  Register #(.width(32)) x1_ra (.D(wdata), .en(decoder_1_out1), .clk(clk), .Q(x1_ra_q), .clr(rst));
  Register #(.width(32)) x2_sp (.D(wdata), .en(decoder_1_out2), .clk(clk), .Q(x2_sp_q), .clr(rst));
  Register #(.width(32)) x3_gp (.D(wdata), .en(decoder_1_out3), .clk(clk), .Q(x3_gp_q), .clr(rst));
  Register #(.width(32)) x4_tp (.D(wdata), .en(decoder_1_out4), .clk(clk), .Q(x4_tp_q), .clr(rst));
  Register #(.width(32)) x5_t0 (.D(wdata), .en(decoder_1_out5), .clk(clk), .Q(x5_t0_q), .clr(rst));
  Register #(.width(32)) x6_t1 (.D(wdata), .en(decoder_1_out6), .clk(clk), .Q(x6_t1_q), .clr(rst));
  Register #(.width(32)) x7_t2 (.D(wdata), .en(decoder_1_out7), .clk(clk), .Q(x7_t2_q), .clr(rst));
  Register #(.width(32)) x8_fp (.D(wdata), .en(decoder_1_out8), .clk(clk), .Q(x8_fp_q), .clr(rst));
  Register #(.width(32)) x9_s1 (.D(wdata), .en(decoder_1_out9), .clk(clk), .Q(x9_s1_q), .clr(rst));
  Register #(.width(32)) x10_a0 (.D(wdata), .en(decoder_1_out10), .clk(clk), .Q(x10_a0_q), .clr(rst));
  Register #(.width(32)) x11_a1 (.D(wdata), .en(decoder_1_out11), .clk(clk), .Q(x11_a1_q), .clr(rst));
  Register #(.width(32)) x12_a2 (.D(wdata), .en(decoder_1_out12), .clk(clk), .Q(x12_a2_q), .clr(rst));
  Register #(.width(32)) x13_a3 (.D(wdata), .en(decoder_1_out13), .clk(clk), .Q(x13_a3_q), .clr(rst));
  Register #(.width(32)) x14_a4 (.D(wdata), .en(decoder_1_out14), .clk(clk), .Q(x14_a4_q), .clr(rst));
  Register #(.width(32)) x15_a5 (.D(wdata), .en(decoder_1_out15), .clk(clk), .Q(x15_a5_q), .clr(rst));
  Multiplexer #(.select(5), .width(32)) multiplexer_1 (
    .in0(x0_zero_q), .in1(x1_ra_q), .in2(x2_sp_q), .in3(x3_gp_q), .in4(x4_tp_q), .in5(x5_t0_q),
    .in6(x6_t1_q), .in7(x7_t2_q), .in8(x8_fp_q), .in9(x9_s1_q), .in10(x10_a0_q), .in11(x11_a1_q),
    .in12(x12_a2_q), .in13(x13_a3_q), .in14(x14_a4_q), .in15(x15_a5_q), .out(rdata1), .sel(radd1));  // open: in16, in17, in18, in19, in20, in21, in22, in23, in24, in25, in26, in27, in28, in29, in30, in31
  Multiplexer #(.select(5), .width(32)) multiplexer_2 (
    .in0(x0_zero_q), .in1(x1_ra_q), .in2(x2_sp_q), .in3(x3_gp_q), .in4(x4_tp_q), .in5(x5_t0_q),
    .in6(x6_t1_q), .in7(x7_t2_q), .in8(x8_fp_q), .in9(x9_s1_q), .in10(x10_a0_q), .in11(x11_a1_q),
    .in12(x12_a2_q), .in13(x13_a3_q), .in14(x14_a4_q), .in15(x15_a5_q), .out(rdata2), .sel(radd2));  // open: in16, in17, in18, in19, in20, in21, in22, in23, in24, in25, in26, in27, in28, in29, in30, in31
endmodule

module miniROM (
  input  [31:0] addr,
  output [31:0] out_2
);

  wire [15:0] bit_extender_1_out;

  Bit_Extender #(.in_width(32), .\type ("zero")) bit_extender_1 (.in(addr), .out(bit_extender_1_out));
  ROM #(.addrWidth(16)) rom_1 (.addr(bit_extender_1_out), .data(out_2[7:0]));
  ROM #(.addrWidth(16)) rom_2 (.addr(bit_extender_1_out), .data(out_2[15:8]));
  ROM #(.addrWidth(16)) rom_3 (.addr(bit_extender_1_out), .data(out_2[23:16]));
  ROM #(.addrWidth(16)) rom_4 (.addr(bit_extender_1_out), .data(out_2[31:24]));

  // Notes on the sheet:
  //   contents of rom_1 (hex, n*v repeats v):
  //   13
  //   contents of rom_2 (hex, n*v repeats v):
  //   13
  //   contents of rom_3 (hex, n*v repeats v):
  //   13
  //   contents of rom_4 (hex, n*v repeats v):
  //   13
endmodule
