// Logisim project Latch.circ as structural Verilog: 11 circuits, main circuit sr_latch
module sr_latch (
  input  r,
  input  s,
  output q,
  output out_4
);

  nor nor_1 (q, r, out_4);
  nor nor_2 (out_4, q, s);
endmodule

module d_latch (
  input  we,
  input  d,
  input  rst,
  output q
);

  wire and_1_out, and_2_out, not_1_out, or_1_out;

  not not_1 (not_1_out, d);
  and and_1 (and_1_out, d, we);
  and and_2 (and_2_out, we, not_1_out);
  or or_1 (or_1_out, and_2_out, rst);
  sr_latch sr_latch_1 (.r(or_1_out), .s(and_1_out), .q(q));  // open: out_4
endmodule

module bit_filp (
  input  in_1,
  input  in_2
);

  wire d_latch_1_q, not_1_out;

  not not_1 (not_1_out, d_latch_1_q);
  d_latch d_latch_1 (.we(in_1), .d(not_1_out), .rst(in_2), .q(d_latch_1_q));
endmodule

module d_flip_flop (
  input  clk,
  input  D,
  input  rst,
  output out_4
);

  wire d_latch_1_q, not_1_out;

  not not_1 (not_1_out, clk);
  d_latch d_latch_1 (.we(not_1_out), .d(D), .rst(rst), .q(d_latch_1_q));
  d_latch d_latch_2 (.we(clk), .d(d_latch_1_q), .rst(rst), .q(out_4));
endmodule

module dff_bit_flip (
  input  clk,
  input  rst
);

  wire d_flip_flop_1_out_4, not_1_out;

  not not_1 (not_1_out, d_flip_flop_1_out_4);
  d_flip_flop d_flip_flop_1 (.clk(clk), .D(not_1_out), .rst(rst), .out_4(d_flip_flop_1_out_4));
endmodule

module d_filp_flop_en (
  input  en,
  input  clk,
  input  D,
  input  rst,
  output Q
);

  wire and_1_out;

  and and_1 (and_1_out, en, clk);
  d_flip_flop d_flip_flop_1 (.clk(and_1_out), .D(D), .rst(rst), .out_4(Q));
endmodule

module register_4bit (
  input  rst,
  input  clk,
  input  en,
  input  [3:0] D,
  output [3:0] Q
);

  d_filp_flop_en d_filp_flop_en_1 (.en(en), .clk(clk), .D(D[0]), .rst(rst), .Q(Q[0]));
  d_filp_flop_en d_filp_flop_en_2 (.en(en), .clk(clk), .D(D[1]), .rst(rst), .Q(Q[1]));
  d_filp_flop_en d_filp_flop_en_3 (.en(en), .clk(clk), .D(D[2]), .rst(rst), .Q(Q[2]));
  d_filp_flop_en d_filp_flop_en_4 (.en(en), .clk(clk), .D(D[3]), .rst(rst), .Q(Q[3]));
endmodule

module counter_4bit (
  input  rst,
  input  clk,
  input  en,
  output [3:0] value
);

  wire [3:0] register_4bit_1_q;

  register_4bit register_4bit_1 (.rst(rst), .clk(clk), .en(en), .D(value), .Q(register_4bit_1_q));
  full_adder_4bit_input full_adder_4bit_input_1 (.a(register_4bit_1_q), .b(4'b0001), .s(value));  // open: cout
endmodule

module sum_1_10 (
  input  rst,
  input  clk,
  input  en
);

  wire full_adder_4bit_input_1_cout;
  wire [3:0] bit_extender_1_out, counter_4bit_1_value, full_adder_4bit_input_1_s, full_adder_4bit_input_2_s,
       register_4bit_1_q, register_4bit_2_q;

  counter_4bit counter_4bit_1 (.rst(rst), .clk(clk), .en(en), .value(counter_4bit_1_value));
  // Probe on counter_4bit_1_value
  // Probe on register_4bit_1_q
  // Probe on register_4bit_2_q
  full_adder_4bit_input full_adder_4bit_input_1 (
    .a(counter_4bit_1_value), .b(register_4bit_1_q), .cout(full_adder_4bit_input_1_cout),
    .s(full_adder_4bit_input_1_s));
  full_adder_4bit_input full_adder_4bit_input_2 (
    .a(bit_extender_1_out), .b(register_4bit_2_q), .s(full_adder_4bit_input_2_s));  // open: cout
  register_4bit register_4bit_1 (.rst(rst), .clk(clk), .en(en), .D(full_adder_4bit_input_1_s), .Q(register_4bit_1_q));
  register_4bit register_4bit_2 (.rst(rst), .clk(clk), .en(en), .D(full_adder_4bit_input_2_s), .Q(register_4bit_2_q));
  assign bit_extender_1_out = {{3{1'b0}}, full_adder_4bit_input_1_cout};  // Bit_Extender bit_extender_1
endmodule

module digital_clock (
  input  rst,
  input  en,
  output [7:0] out_3,
  output [7:0] out_4
);

  wire clock_1_out, comparator_1_lt, not_1_out;
  wire [7:0] adder_1_out, adder_2_out, multiplexer_1_out, multiplexer_2_out, subtractor_1_out;

  Clock clock_1 (.out(clock_1_out));
  Subtractor subtractor_1 (.a(adder_1_out), .b(8'h3c), .out(subtractor_1_out));  // open: bin, bout
  Comparator comparator_1 (.a(adder_1_out), .b(8'h3c), .lt(comparator_1_lt));  // open: gt, eq
  Multiplexer #(.width(8)) multiplexer_1 (
    .in0(subtractor_1_out), .in1(adder_1_out), .out(multiplexer_1_out), .sel(comparator_1_lt));
  Multiplexer #(.width(8)) multiplexer_2 (.in0(out_4), .in1(adder_2_out), .out(multiplexer_2_out), .sel(not_1_out));
  Adder adder_1 (.a(out_3), .b(8'h1), .out(adder_1_out));  // open: cin, cout
  not not_1 (not_1_out, comparator_1_lt);
  Register second (.D(multiplexer_1_out), .en(en), .clk(clock_1_out), .Q(out_3), .clr(rst));
  Register min (.D(multiplexer_2_out), .en(en), .clk(clock_1_out), .Q(out_4), .clr(rst));
  Adder adder_2 (.a(out_4), .b(8'h1), .out(adder_2_out));  // open: cin, cout
endmodule

module counter_8bit (
  input  rst,
  input  clk,
  input  en,
  output [7:0] out_4
);

  wire [7:0] register_1_q;

  Register register_1 (.D(out_4), .en(en), .clk(clk), .Q(register_1_q), .clr(rst));
  Adder adder_1 (.a(register_1_q), .b(8'h1), .out(out_4));  // open: cin, cout
endmodule
