// Logisim project comparator_4bit.circ as structural Verilog: 2 circuits, main circuit my_comparator
module my_comparator (
  input  in_1,
  input  in_2,
  input  in_3,
  input  in_4,
  input  in_5,
  input  in_6,
  input  in_7,
  input  in_8,
  output out_9
);

  wire not_1_out, not_2_out, not_3_out, not_4_out, xor_1_out, xor_2_out, xor_3_out, xor_4_out;

  xor xor_1 (xor_1_out, in_1, in_2);
  xor xor_2 (xor_2_out, in_3, in_4);
  xor xor_3 (xor_3_out, in_5, in_6);
  xor xor_4 (xor_4_out, in_7, in_8);
  not not_1 (not_1_out, xor_1_out);
  not not_2 (not_2_out, xor_2_out);
  not not_3 (not_3_out, xor_3_out);
  not not_4 (not_4_out, xor_4_out);
  and and_1 (out_9, not_1_out, not_2_out, not_3_out, not_4_out);
endmodule

module test_comparator (
);

  wire dipswitch_1_sw1, dipswitch_1_sw2, dipswitch_1_sw3, dipswitch_1_sw4, dipswitch_2_sw1, dipswitch_2_sw2,
       dipswitch_2_sw3, dipswitch_2_sw4, my_comparator_1_out_9;

  DipSwitch #(.number(4)) dipswitch_1 (
    .sw1(dipswitch_1_sw1), .sw2(dipswitch_1_sw2), .sw3(dipswitch_1_sw3), .sw4(dipswitch_1_sw4));
  DipSwitch #(.number(4)) dipswitch_2 (
    .sw1(dipswitch_2_sw1), .sw2(dipswitch_2_sw2), .sw3(dipswitch_2_sw3), .sw4(dipswitch_2_sw4));
  LED led_1 (.in(my_comparator_1_out_9));
  my_comparator my_comparator_1 (
    .in_1(dipswitch_1_sw1), .in_2(dipswitch_2_sw1), .in_3(dipswitch_1_sw2), .in_4(dipswitch_2_sw2),
    .in_5(dipswitch_1_sw3), .in_6(dipswitch_2_sw3), .in_7(dipswitch_1_sw4), .in_8(dipswitch_2_sw4),
    .out_9(my_comparator_1_out_9));
endmodule
