// Logisim project decoder38.circ as structural Verilog: 2 circuits, main circuit main
module decoder24 (
  input  in_1,
  input  in_2,
  output out_3,
  output out_4,
  output out_5,
  output out_6
);

  wire not_1_out, not_2_out;

  not not_1 (not_1_out, in_1);
  not not_2 (not_2_out, in_2);
  and and_1 (out_3, not_1_out, not_2_out);
  and and_2 (out_4, not_1_out, in_2);
  and and_3 (out_5, in_1, not_2_out);
  and and_4 (out_6, in_1, in_2);
endmodule

module main (
  input  in_1,
  input  in_2,
  input  in_3,
  output out_4,
  output out_5,
  output out_6,
  output out_7,
  output out_8,
  output out_9,
  output out_10,
  output out_11
);

  wire decoder24_1_out_3, decoder24_1_out_4, decoder24_1_out_5, decoder24_1_out_6, decoder24_2_out_3,
       decoder24_2_out_4, decoder24_2_out_5, decoder24_2_out_6, not_1_out;

  not not_1 (not_1_out, in_3);
  decoder24 decoder24_1 (
    .in_1(in_1), .in_2(in_2), .out_3(decoder24_1_out_3), .out_4(decoder24_1_out_4),
    .out_5(decoder24_1_out_5), .out_6(decoder24_1_out_6));
  decoder24 decoder24_2 (
    .in_1(in_1), .in_2(in_2), .out_3(decoder24_2_out_3), .out_4(decoder24_2_out_4),
    .out_5(decoder24_2_out_5), .out_6(decoder24_2_out_6));
  and and_1 (out_4, in_3, decoder24_1_out_3);
  and and_2 (out_8, decoder24_2_out_3, not_1_out);
  and and_3 (out_5, in_3, decoder24_1_out_4);
  and and_4 (out_10, decoder24_2_out_4, not_1_out);
  and and_5 (out_6, in_3, decoder24_1_out_5);
  and and_6 (out_9, decoder24_2_out_5, not_1_out);
  and and_7 (out_7, in_3, decoder24_1_out_6);
  and and_8 (out_11, decoder24_2_out_6, not_1_out);
endmodule
