// Logisim project encoder164.circ as structural Verilog: 2 circuits, main circuit main
module main (
  input  in_1,
  input  in_2,
  input  in_3,
  input  in_4,
  input  in_5,
  input  in_6,
  input  in_7,
  input  in_8,
  input  in_9,
  input  in_10,
  input  in_11,
  input  in_12,
  input  in_13,
  input  in_14,
  input  in_15,
  input  in_16
);

  wire encoder16_4_1_y0, encoder16_4_1_y1, encoder16_4_1_y2, encoder16_4_1_y3;

  encoder16_4 encoder16_4_1 (
    .a1(in_2), .a2(in_3), .a3(in_4), .a4(in_5), .a5(in_6), .a6(in_7), .a7(in_8), .a8(in_9), .a9(in_10),
    .a10(in_11), .a11(in_12), .a12(in_13), .a13(in_14), .a14(in_15), .a15(in_16), .a0(in_1),
    .y3(encoder16_4_1_y3), .y0(encoder16_4_1_y0), .y1(encoder16_4_1_y1), .y2(encoder16_4_1_y2));
  segment7_input segment7_input_1 (
    .in_1(encoder16_4_1_y3), .in_2(encoder16_4_1_y2), .in_3(encoder16_4_1_y1), .in_4(encoder16_4_1_y0));
endmodule

module encoder16_4 (
  input  a0,
  input  a1,
  input  a2,
  input  a3,
  input  a4,
  input  a5,
  input  a6,
  input  a7,
  input  a8,
  input  a9,
  input  a10,
  input  a11,
  input  a12,
  input  a13,
  input  a14,
  input  a15,
  output y0,
  output y2,
  output y3,
  output y1
);

  or or_1 (y0, a1, a3, a5, a7, a9, a11, a13, a15);
  or or_2 (y1, a2, a6, a10, a14, a3, a7, a11, a15);
  or or_3 (y2, a4, a5, a6, a7, a12, a13, a14, a15);
  or or_4 (y3, a8, a9, a10, a11, a12, a13, a14, a15);
endmodule
