// Logisim project full_adder_4bit.circ as structural Verilog: 3 circuits, main circuit full_adder_4bit
module full_adder_4bit (
);

  wire dipswitch_1_sw1, dipswitch_1_sw2, dipswitch_1_sw3, dipswitch_1_sw4, dipswitch_2_sw1, dipswitch_2_sw2,
       dipswitch_2_sw3, dipswitch_2_sw4, full_adder_1_cout, full_adder_1_s, full_adder_2_cout,
       full_adder_2_s, full_adder_3_cout, full_adder_3_s, full_adder_4_cout, full_adder_4_s;

  DipSwitch #(.number(4)) dipswitch_1 (
    .sw1(dipswitch_1_sw1), .sw2(dipswitch_1_sw2), .sw3(dipswitch_1_sw3), .sw4(dipswitch_1_sw4));
  DipSwitch #(.number(4)) dipswitch_2 (
    .sw1(dipswitch_2_sw1), .sw2(dipswitch_2_sw2), .sw3(dipswitch_2_sw3), .sw4(dipswitch_2_sw4));
  full_adder full_adder_1 (
    .a(dipswitch_2_sw4), .b(dipswitch_1_sw4), .cin(full_adder_2_cout), .cout(full_adder_1_cout),
    .s(full_adder_1_s));
  full_adder full_adder_2 (
    .a(dipswitch_2_sw3), .b(dipswitch_1_sw3), .cin(full_adder_3_cout), .cout(full_adder_2_cout),
    .s(full_adder_2_s));
  full_adder full_adder_3 (
    .a(dipswitch_2_sw2), .b(dipswitch_1_sw2), .cin(full_adder_4_cout), .cout(full_adder_3_cout),
    .s(full_adder_3_s));
  full_adder full_adder_4 (
    .a(dipswitch_2_sw1), .b(dipswitch_1_sw1), .cin(1'b0), .cout(full_adder_4_cout), .s(full_adder_4_s));
  segment7_input segment7_input_1 (
    .in_1(full_adder_1_s), .in_2(full_adder_2_s), .in_3(full_adder_3_s), .in_4(full_adder_4_s));
  LED led_1 (.in(full_adder_1_cout));
endmodule

module full_adder_4bit_input (
  input  [3:0] a,
  input  [3:0] b,
  output [3:0] s,
  output cout
);

  wire full_adder_2_cout, full_adder_3_cout, full_adder_4_cout;

  full_adder full_adder_1 (.a(b[3]), .b(a[3]), .cin(full_adder_2_cout), .cout(cout), .s(s[3]));
  full_adder full_adder_2 (.a(b[2]), .b(a[2]), .cin(full_adder_3_cout), .cout(full_adder_2_cout), .s(s[2]));
  full_adder full_adder_3 (.a(b[1]), .b(a[1]), .cin(full_adder_4_cout), .cout(full_adder_3_cout), .s(s[1]));
  full_adder full_adder_4 (.a(b[0]), .b(a[0]), .cin(1'b0), .cout(full_adder_4_cout), .s(s[0]));
endmodule

module full_adder_4bit_overflow (
  input  [3:0] a,
  input  [3:0] b,
  output out_3,
  output [3:0] s,
  output cout
);

  wire and_1_out, and_2_out, full_adder_2_cout, full_adder_3_cout, full_adder_4_cout;

  full_adder full_adder_1 (.a(b[3]), .b(a[3]), .cin(full_adder_2_cout), .cout(cout), .s(s[3]));
  full_adder full_adder_2 (.a(b[2]), .b(a[2]), .cin(full_adder_3_cout), .cout(full_adder_2_cout), .s(s[2]));
  full_adder full_adder_3 (.a(b[1]), .b(a[1]), .cin(full_adder_4_cout), .cout(full_adder_3_cout), .s(s[1]));
  full_adder full_adder_4 (.a(b[0]), .b(a[0]), .cin(1'b0), .cout(full_adder_4_cout), .s(s[0]));
  and and_1 (and_1_out, ~a[3], ~b[3], s[3]);  // AND_Gate
  and and_2 (and_2_out, a[3], b[3], ~s[3]);  // AND_Gate
  or or_1 (out_3, and_1_out, and_2_out);
endmodule
