// Logisim project full_suber.circ as structural Verilog: 1 circuit, main circuit full_sub
module full_sub (
  input  a,
  input  b,
  input  bin,
  output d,
  output bout
);

  wire and_1_out, and_2_out, not_1_out, not_2_out, xor_1_out;

  xor xor_1 (xor_1_out, a, b);
  not not_1 (not_1_out, xor_1_out);
  not not_2 (not_2_out, a);
  xor xor_2 (d, xor_1_out, bin);
  and and_1 (and_1_out, not_1_out, bin);
  and and_2 (and_2_out, not_2_out, b);
  or or_1 (bout, and_1_out, and_2_out);
endmodule
