// Logisim project full_suber_4bit.circ as structural Verilog: 2 circuits, main circuit full_suber_4bit
module full_suber_4bit (
);

  wire dipswitch_1_sw1, dipswitch_1_sw2, dipswitch_1_sw3, dipswitch_1_sw4, dipswitch_2_sw1, dipswitch_2_sw2,
       dipswitch_2_sw3, dipswitch_2_sw4, full_sub_1_bout, full_sub_1_d, full_sub_2_bout, full_sub_2_d,
       full_sub_3_bout, full_sub_3_d, full_sub_4_bout, full_sub_4_d;

  DipSwitch #(.number(4)) dipswitch_1 (
    .sw1(dipswitch_1_sw1), .sw2(dipswitch_1_sw2), .sw3(dipswitch_1_sw3), .sw4(dipswitch_1_sw4));
  DipSwitch #(.number(4)) dipswitch_2 (
    .sw1(dipswitch_2_sw1), .sw2(dipswitch_2_sw2), .sw3(dipswitch_2_sw3), .sw4(dipswitch_2_sw4));
  full_sub full_sub_1 (
    .a(dipswitch_1_sw4), .b(dipswitch_2_sw4), .bin(full_sub_2_bout), .d(full_sub_1_d), .bout(full_sub_1_bout));
  full_sub full_sub_2 (
    .a(dipswitch_1_sw3), .b(dipswitch_2_sw3), .bin(full_sub_3_bout), .d(full_sub_2_d), .bout(full_sub_2_bout));
  full_sub full_sub_3 (
    .a(dipswitch_1_sw2), .b(dipswitch_2_sw2), .bin(full_sub_4_bout), .d(full_sub_3_d), .bout(full_sub_3_bout));
  full_sub full_sub_4 (.a(dipswitch_1_sw1), .b(dipswitch_2_sw1), .bin(1'b0), .d(full_sub_4_d), .bout(full_sub_4_bout));
  segment7_input segment7_input_1 (.in_1(full_sub_1_d), .in_2(full_sub_2_d), .in_3(full_sub_3_d), .in_4(full_sub_4_d));
  LED led_1 (.in(full_sub_1_bout));
endmodule

module full_suber_4bit_input (
  input  [3:0] a,
  input  [3:0] b,
  output [3:0] d,
  output bout
);

  wire full_sub_2_bout, full_sub_3_bout, full_sub_4_bout;

  full_sub full_sub_1 (.a(a[3]), .b(b[3]), .bin(full_sub_2_bout), .d(d[3]), .bout(bout));
  full_sub full_sub_2 (.a(a[2]), .b(b[2]), .bin(full_sub_3_bout), .d(d[2]), .bout(full_sub_2_bout));
  full_sub full_sub_3 (.a(a[1]), .b(b[1]), .bin(full_sub_4_bout), .d(d[1]), .bout(full_sub_3_bout));
  full_sub full_sub_4 (.a(a[0]), .b(b[0]), .bin(1'b0), .d(d[0]), .bout(full_sub_4_bout));
endmodule
