// Logisim project mux21_1bit.circ as structural Verilog: 1 circuit, main circuit mux21
module mux21 (
  input  in_1,
  input  in_2,
  input  in_3,
  output out_4
);

  wire and_1_out, and_2_out, not_1_out;

  not not_1 (not_1_out, in_2);
  and and_1 (and_1_out, in_1, not_1_out);
  and and_2 (and_2_out, in_2, in_3);
  // OR_Gate or_1 has open pins: in0=and_1_out, in1=and_2_out, out=open
endmodule
