// Logisim project mux41_3bit.circ as structural Verilog: 1 circuit, main circuit mux41
module mux41 (
  input  in_1,
  input  in_2,
  input  in_3,
  input  in_4,
  input  in_5,
  input  in_6,
  input  in_7,
  input  in_8,
  input  in_9,
  input  in_10,
  input  in_11,
  input  in_12,
  input  s0,
  input  s1,
  output out_15,
  output out_16,
  output out_17
);

  wire and_1_out, and_2_out, and_3_out, and_4_out, and_5_out, and_6_out, and_7_out, and_8_out, and_9_out,
       and_10_out, and_11_out, and_12_out, decode24_1_out_3, decode24_1_out_4, decode24_1_out_5,
       decode24_1_out_6;

  decode24 decode24_1 (
    .in_1(s0), .in_2(s1), .out_4(decode24_1_out_4), .out_5(decode24_1_out_5), .out_6(decode24_1_out_6),
    .out_3(decode24_1_out_3));
  and and_1 (and_1_out, in_1, decode24_1_out_3);
  and and_2 (and_2_out, in_4, decode24_1_out_4);
  and and_3 (and_3_out, in_7, decode24_1_out_5);
  or or_1 (out_15, and_1_out, and_2_out, and_3_out, and_4_out);
  and and_4 (and_4_out, in_10, decode24_1_out_6);
  and and_5 (and_5_out, in_2, decode24_1_out_3);
  and and_6 (and_6_out, in_5, decode24_1_out_4);
  and and_7 (and_7_out, in_8, decode24_1_out_5);
  or or_2 (out_16, and_5_out, and_6_out, and_7_out, and_8_out);
  and and_8 (and_8_out, in_11, decode24_1_out_6);
  and and_9 (and_9_out, in_3, decode24_1_out_3);
  and and_10 (and_10_out, in_6, decode24_1_out_4);
  or or_3 (out_17, and_9_out, and_10_out, and_11_out, and_12_out);
  and and_11 (and_11_out, in_9, decode24_1_out_5);
  and and_12 (and_12_out, in_12, decode24_1_out_6);
endmodule
