// Logisim project prio_encoder164.circ as structural Verilog: 2 circuits, main circuit encoder164_prio
module encoder164_prio (
  input  in_1,
  input  in_2,
  input  in_3,
  input  in_4,
  input  in_5,
  input  in_6,
  input  in_7,
  input  in_8,
  input  in_9,
  input  in_10,
  input  in_11,
  input  in_12,
  input  in_13,
  input  in_14,
  input  in_15,
  input  in_16,
  output valid,
  output y3,
  output y2,
  output y1,
  output y0
);

  wire and_1_out, and_2_out, and_3_out, and_4_out, and_5_out, and_6_out, and_7_out, and_8_out, and_9_out,
       and_10_out, and_11_out, and_12_out, encoder42_prio_1_valid, encoder42_prio_1_y0, encoder42_prio_1_y1,
       encoder42_prio_2_valid, encoder42_prio_2_y0, encoder42_prio_2_y1, encoder42_prio_3_valid,
       encoder42_prio_3_y0, encoder42_prio_3_y1, encoder42_prio_4_valid, encoder42_prio_4_y0,
       encoder42_prio_4_y1, encoder42_prio_5_y0, encoder42_prio_5_y1;

  encoder42_prio encoder42_prio_1 (
    .a3(in_4), .a2(in_3), .a1(in_2), .a0(in_1), .y0(encoder42_prio_1_y0), .valid(encoder42_prio_1_valid),
    .y1(encoder42_prio_1_y1));
  encoder42_prio encoder42_prio_2 (
    .a3(in_8), .a2(in_7), .a1(in_6), .a0(in_5), .y0(encoder42_prio_2_y0), .valid(encoder42_prio_2_valid),
    .y1(encoder42_prio_2_y1));
  encoder42_prio encoder42_prio_3 (
    .a3(in_12), .a2(in_11), .a1(in_10), .a0(in_9), .y0(encoder42_prio_3_y0), .valid(encoder42_prio_3_valid),
    .y1(encoder42_prio_3_y1));
  encoder42_prio encoder42_prio_4 (
    .a3(in_16), .a2(in_15), .a1(in_14), .a0(in_13), .y0(encoder42_prio_4_y0), .valid(encoder42_prio_4_valid),
    .y1(encoder42_prio_4_y1));
  encoder42_prio encoder42_prio_5 (
    .a3(encoder42_prio_4_valid), .a2(encoder42_prio_3_valid), .a1(encoder42_prio_2_valid),
    .a0(encoder42_prio_1_valid), .y0(encoder42_prio_5_y0), .valid(valid), .y1(encoder42_prio_5_y1));
  or or_1 (y3, encoder42_prio_4_valid, encoder42_prio_3_valid);
  and and_1 (and_1_out, ~encoder42_prio_5_y0, ~encoder42_prio_5_y1);  // AND_Gate
  and and_2 (and_2_out, encoder42_prio_5_y0, ~encoder42_prio_5_y1);  // AND_Gate
  and and_3 (and_3_out, ~encoder42_prio_5_y0, encoder42_prio_5_y1);  // AND_Gate
  and and_4 (and_4_out, encoder42_prio_5_y0, encoder42_prio_5_y0);
  or or_2 (y2, and_2_out, encoder42_prio_4_valid);
  and and_5 (and_5_out, encoder42_prio_4_y1, and_4_out);
  and and_6 (and_6_out, encoder42_prio_3_y1, and_3_out);
  or or_3 (y1, and_5_out, and_6_out, and_7_out, and_8_out);
  and and_7 (and_7_out, encoder42_prio_2_y1, and_2_out);
  and and_8 (and_8_out, encoder42_prio_1_y1, and_1_out);
  and and_9 (and_9_out, encoder42_prio_1_y0, and_1_out);
  or or_4 (y0, and_9_out, and_10_out, and_11_out, and_12_out);
  and and_10 (and_10_out, encoder42_prio_2_y0, and_2_out);
  and and_11 (and_11_out, encoder42_prio_3_y0, and_3_out);
  and and_12 (and_12_out, encoder42_prio_4_y0, and_4_out);
endmodule

module test_encoder164_prio (
  input  in_1,
  input  in_2,
  input  in_3,
  input  in_4,
  input  in_5,
  input  in_6,
  input  in_7,
  input  in_8,
  input  in_9,
  input  in_10,
  input  in_11,
  input  in_12,
  input  in_13,
  input  in_14,
  input  in_15,
  input  in_16
);

  wire encoder164_prio_1_y0, encoder164_prio_1_y1, encoder164_prio_1_y2, encoder164_prio_1_y3;

  encoder164_prio encoder164_prio_1 (
    .in_1(in_1), .in_2(in_2), .in_3(in_3), .in_4(in_4), .in_5(in_5), .in_6(in_6), .in_7(in_7), .in_8(in_8),
    .in_9(in_9), .in_10(in_10), .in_11(in_11), .in_12(in_12), .in_13(in_13), .in_14(in_14), .in_15(in_15),
    .in_16(in_16), .y3(encoder164_prio_1_y3), .y2(encoder164_prio_1_y2), .y1(encoder164_prio_1_y1),
    .y0(encoder164_prio_1_y0));  // open: valid
  segment7_input segment7_input_1 (
    .in_1(encoder164_prio_1_y3), .in_2(encoder164_prio_1_y2), .in_3(encoder164_prio_1_y1),
    .in_4(encoder164_prio_1_y0));
endmodule
