// Logisim project prio_encoder42.circ as structural Verilog: 1 circuit, main circuit encoder42_prio
module encoder42_prio (
  input  a3,
  input  a2,
  input  a1,
  input  a0,
  output y1,
  output y0,
  output valid
);

  wire and_1_out, and_2_out, and_3_out, not_1_out, not_2_out, not_3_out, not_4_out;

  not not_1 (not_1_out, a3);
  not not_2 (not_2_out, a2);
  not not_3 (not_3_out, a1);
  not not_4 (not_4_out, a0);
  and and_1 (and_1_out, not_1_out, a2);
  or or_1 (y1, and_1_out, a3);
  and and_2 (and_2_out, not_1_out, not_2_out, a1);
  or or_2 (y0, and_2_out, a3);
  and and_3 (and_3_out, not_1_out, not_2_out, not_3_out, not_4_out);
  not not_5 (valid, and_3_out);
endmodule
