// Logisim project sCpu.circ as structural Verilog: 4 circuits, main circuit main
module main (
  input  rst,
  input  clk
);

  wire and_1_out, comparator_1_eq, decoder_1_out0, decoder_1_out1, decoder_1_out2, decoder_1_out3, not_1_out,
       or_1_out;
  wire [1:0] multiplexer_1_out;
  wire [3:0] pc_q, srom_1_inst;
  wire [7:0] adder_1_out, and_2_out, bit_extender_1_out, bit_extender_2_out, multiplexer_2_out,
       sgpr_1_rdata1, sgpr_1_rdata2, srom_1_inst_2;

  sRom srom_1 (.pc(pc_q), .inst({srom_1_inst_2[7:6], srom_1_inst, srom_1_inst_2[1:0]}));
  Counter #(.max('hf), .width(4)) pc (
    .load(and_1_out), .D(srom_1_inst), .count(1'b1), .Q(pc_q), .up(1'b1), .clk(clk), .clr(rst));  // open: carry
  assign bit_extender_1_out = {{4{1'b0}}, {srom_1_inst[1:0], srom_1_inst_2[1:0]}};  // Bit_Extender bit_extender_1
  Decoder #(.select(2)) decoder_1 (
    .out0(decoder_1_out0), .out1(decoder_1_out1), .out2(decoder_1_out2), .out3(decoder_1_out3),
    .sel(srom_1_inst_2[7:6]));  // open: en
  and and_1 (and_1_out, decoder_1_out3, not_1_out);
  Multiplexer #(.width(2)) multiplexer_1 (
    .in0(srom_1_inst[1:0]), .in1(2'b00), .out(multiplexer_1_out), .sel(decoder_1_out3));
  Multiplexer #(.width(8)) multiplexer_2 (
    .in0(adder_1_out), .in1(bit_extender_1_out), .out(multiplexer_2_out), .sel(decoder_1_out2));
  or or_1 (or_1_out, decoder_1_out2, decoder_1_out0);
  sGPR sgpr_1 (
    .raddr1(multiplexer_1_out), .rst(rst), .raddr2(srom_1_inst_2[1:0]), .we(or_1_out),
    .waddr(srom_1_inst[3:2]), .clk(clk), .wdata(multiplexer_2_out), .rdata1(sgpr_1_rdata1),
    .rdata2(sgpr_1_rdata2));
  Adder adder_1 (.a(sgpr_1_rdata1), .b(sgpr_1_rdata2), .out(adder_1_out));  // open: cin, cout
  not not_1 (not_1_out, comparator_1_eq);
  Comparator comparator_1 (.a(sgpr_1_rdata1), .b(sgpr_1_rdata2), .eq(comparator_1_eq));  // open: gt, lt
  assign bit_extender_2_out = {{7{decoder_1_out1}}, decoder_1_out1};  // Bit_Extender bit_extender_2
  assign and_2_out = bit_extender_2_out & sgpr_1_rdata1;  // AND_Gate and_2, 8 bits wide
  Hex_Digit_Display hex_digit_display_1 (.value(and_2_out[7:4]));  // open: dp
  Hex_Digit_Display hex_digit_display_2 (.value(and_2_out[3:0]));  // open: dp
endmodule

module sRom (
  input  [3:0] pc,
  output [7:0] inst
);

  Multiplexer #(.select(4), .width(8)) multiplexer_1 (
    .in0(8'h89), .in1(8'h91), .in2(8'ha1), .in3(8'hb2), .in4(8'h17), .in5(8'h29), .in6(8'hd1), .in7(8'h48),
    .in8(8'hdf), .in9({8{1'b0}}), .in10({8{1'b0}}), .in11({8{1'b0}}), .in12({8{1'b0}}), .in13({8{1'b0}}),
    .in14({8{1'b0}}), .in15({8{1'b0}}), .out(inst), .sel(pc));
endmodule

module sGPR (
  input  clk,
  input  [7:0] wdata,
  input  [1:0] raddr1,
  input  rst,
  input  [1:0] waddr,
  input  we,
  input  [1:0] raddr2,
  output [7:0] rdata1,
  output [7:0] rdata2
);

  wire and_1_out, and_2_out, and_3_out, and_4_out, decoder_1_out0, decoder_1_out1, decoder_1_out2,
       decoder_1_out3;
  wire [7:0] register_1_q, register_2_q, register_3_q, register_4_q;

  Decoder #(.select(2)) decoder_1 (
    .out0(decoder_1_out0), .out1(decoder_1_out1), .out2(decoder_1_out2), .out3(decoder_1_out3), .sel(waddr));  // open: en
  and and_1 (and_1_out, decoder_1_out1, we);
  and and_2 (and_2_out, decoder_1_out2, we);
  and and_3 (and_3_out, decoder_1_out0, we);
  and and_4 (and_4_out, decoder_1_out3, we);
  Register register_1 (.D(wdata), .en(and_3_out), .clk(clk), .Q(register_1_q), .clr(rst));
  Register register_2 (.D(wdata), .en(and_1_out), .clk(clk), .Q(register_2_q), .clr(rst));
  Register register_3 (.D(wdata), .en(and_2_out), .clk(clk), .Q(register_3_q), .clr(rst));
  Register register_4 (.D(wdata), .en(and_4_out), .clk(clk), .Q(register_4_q), .clr(rst));
  Multiplexer #(.select(2), .width(8)) multiplexer_1 (
    .in0(register_1_q), .in1(register_2_q), .in2(register_3_q), .in3(register_4_q), .out(rdata1), .sel(raddr1));
  Multiplexer #(.select(2), .width(8)) multiplexer_2 (
    .in0(register_1_q), .in1(register_2_q), .in2(register_3_q), .in3(register_4_q), .out(rdata2), .sel(raddr2));
endmodule

module sDecoder (
  input  [7:0] inst,
  output rs1,
  output rs2
);
endmodule
