// Logisim project segmenthex.circ as structural Verilog: 4 circuits, main circuit segment7
module segment7 (
);

  wire decoder48_1_a1, decoder48_1_b1, decoder48_1_c1, decoder48_1_d1, decoder48_1_e1, decoder48_1_f1,
       decoder48_1_g1, dipswitch_1_p1, dipswitch_1_p2, dipswitch_1_p3, dipswitch_1_p4;

  // DipSwitch #(.number(4)) dipswitch_1: pin names not known; wires that end beside it: dipswitch_1_p1, dipswitch_1_p2, dipswitch_1_p3, dipswitch_1_p4
  decoder48 decoder48_1 (
    .in_1(dipswitch_1_p1), .in_2(dipswitch_1_p2), .in_3(dipswitch_1_p3), .in_4(dipswitch_1_p4),
    .a1(decoder48_1_a1), .b1(decoder48_1_b1), .c1(decoder48_1_c1), .d1(decoder48_1_d1), .e1(decoder48_1_e1),
    .f1(decoder48_1_f1), .g1(decoder48_1_g1));
  _7_Segment_Display u_7_segment_display_1 (
    .g(decoder48_1_g1), .f(decoder48_1_f1), .a(decoder48_1_a1), .b(decoder48_1_b1), .e(decoder48_1_e1),
    .d(decoder48_1_d1), .c(decoder48_1_c1));  // open: dp
endmodule

module decoder48 (
  input  in_1,
  input  in_2,
  input  in_3,
  input  in_4,
  output a1,
  output b1,
  output c1,
  output e1,
  output g1,
  output d1,
  output f1
);

  wire binarydecoder_1_out_5, binarydecoder_1_out_6, binarydecoder_1_out_7, binarydecoder_1_out_8,
       binarydecoder_1_out_9, binarydecoder_1_out_10, binarydecoder_1_out_11, binarydecoder_1_out_12,
       binarydecoder_1_out_13, binarydecoder_1_out_14, binarydecoder_1_out_15, binarydecoder_1_out_16,
       binarydecoder_1_out_17, binarydecoder_1_out_18, binarydecoder_1_out_19, binarydecoder_1_out_20;

  binarydecoder binarydecoder_1 (
    .in_1(in_1), .in_2(in_2), .in_3(in_3), .in_4(in_4), .out_5(binarydecoder_1_out_5),
    .out_6(binarydecoder_1_out_6), .out_7(binarydecoder_1_out_7), .out_8(binarydecoder_1_out_8),
    .out_9(binarydecoder_1_out_9), .out_10(binarydecoder_1_out_10), .out_11(binarydecoder_1_out_11),
    .out_12(binarydecoder_1_out_12), .out_13(binarydecoder_1_out_13), .out_14(binarydecoder_1_out_14),
    .out_15(binarydecoder_1_out_15), .out_16(binarydecoder_1_out_16), .out_17(binarydecoder_1_out_17),
    .out_18(binarydecoder_1_out_18), .out_19(binarydecoder_1_out_19), .out_20(binarydecoder_1_out_20));
  or a (a1, binarydecoder_1_out_5, binarydecoder_1_out_7, binarydecoder_1_out_8, binarydecoder_1_out_10, binarydecoder_1_out_11, binarydecoder_1_out_12, binarydecoder_1_out_13, binarydecoder_1_out_14, binarydecoder_1_out_15, binarydecoder_1_out_17, binarydecoder_1_out_19, binarydecoder_1_out_20);
  or b (b1, binarydecoder_1_out_5, binarydecoder_1_out_6, binarydecoder_1_out_7, binarydecoder_1_out_8, binarydecoder_1_out_9, binarydecoder_1_out_12, binarydecoder_1_out_13, binarydecoder_1_out_14, binarydecoder_1_out_15, binarydecoder_1_out_18);
  or c (c1, binarydecoder_1_out_5, binarydecoder_1_out_6, binarydecoder_1_out_8, binarydecoder_1_out_9, binarydecoder_1_out_10, binarydecoder_1_out_11, binarydecoder_1_out_12, binarydecoder_1_out_13, binarydecoder_1_out_14, binarydecoder_1_out_15, binarydecoder_1_out_16, binarydecoder_1_out_18);
  or d (d1, binarydecoder_1_out_5, binarydecoder_1_out_7, binarydecoder_1_out_8, binarydecoder_1_out_10, binarydecoder_1_out_11, binarydecoder_1_out_13, binarydecoder_1_out_14, binarydecoder_1_out_16, binarydecoder_1_out_17, binarydecoder_1_out_17, binarydecoder_1_out_18, binarydecoder_1_out_19);
  or e (e1, binarydecoder_1_out_5, binarydecoder_1_out_7, binarydecoder_1_out_11, binarydecoder_1_out_13, binarydecoder_1_out_15, binarydecoder_1_out_16, binarydecoder_1_out_17, binarydecoder_1_out_18, binarydecoder_1_out_18, binarydecoder_1_out_19, binarydecoder_1_out_20);
  or f (f1, binarydecoder_1_out_5, binarydecoder_1_out_9, binarydecoder_1_out_10, binarydecoder_1_out_11, binarydecoder_1_out_12, binarydecoder_1_out_13, binarydecoder_1_out_14, binarydecoder_1_out_15, binarydecoder_1_out_16, binarydecoder_1_out_17, binarydecoder_1_out_19, binarydecoder_1_out_20);
  or g (g1, binarydecoder_1_out_7, binarydecoder_1_out_8, binarydecoder_1_out_9, binarydecoder_1_out_10, binarydecoder_1_out_11, binarydecoder_1_out_13, binarydecoder_1_out_15, binarydecoder_1_out_16, binarydecoder_1_out_18, binarydecoder_1_out_19, binarydecoder_1_out_20, binarydecoder_1_out_14);
endmodule

module binarydecoder (
  input  in_1,
  input  in_2,
  input  in_3,
  input  in_4,
  output out_5,
  output out_6,
  output out_7,
  output out_8,
  output out_9,
  output out_10,
  output out_11,
  output out_12,
  output out_13,
  output out_14,
  output out_15,
  output out_16,
  output out_17,
  output out_18,
  output out_19,
  output out_20
);

  wire not_1_out, not_2_out, not_3_out, not_4_out;

  not not_1 (not_1_out, in_2);
  not not_2 (not_2_out, in_3);
  not not_3 (not_3_out, in_1);
  not not_4 (not_4_out, in_4);
  and and_1 (out_5, not_3_out, not_1_out, not_2_out, not_4_out);
  and and_2 (out_6, not_3_out, not_1_out, not_2_out, in_4);
  and and_3 (out_7, not_3_out, not_1_out, in_3, not_4_out);
  and and_4 (out_8, not_3_out, not_1_out, in_3, in_4);
  and and_5 (out_9, not_3_out, in_2, not_2_out, not_4_out);
  and and_6 (out_10, not_3_out, in_2, not_2_out, in_4);
  and and_7 (out_11, not_3_out, in_2, in_3, not_4_out);
  and and_8 (out_12, not_3_out, in_2, in_3, in_4);
  and and_9 (out_13, in_1, not_1_out, not_2_out, not_4_out);
  and and_10 (out_14, in_1, not_1_out, not_2_out, in_4);
  and and_11 (out_15, in_1, not_1_out, in_3, not_4_out);
  and and_12 (out_16, in_1, not_1_out, in_3, in_4);
  and and_13 (out_17, in_1, in_2, not_2_out, not_4_out);
  and and_14 (out_18, in_1, in_2, not_2_out, in_4);
  and and_15 (out_19, in_1, in_2, in_3, not_4_out);
  and and_16 (out_20, in_1, in_2, in_3, in_4);
endmodule

module segment7_input (
  input  in_1,
  input  in_2,
  input  in_3,
  input  in_4
);

  wire decoder48_1_a1, decoder48_1_b1, decoder48_1_c1, decoder48_1_d1, decoder48_1_e1, decoder48_1_f1,
       decoder48_1_g1;

  decoder48 decoder48_1 (
    .in_1(in_1), .in_2(in_2), .in_3(in_3), .in_4(in_4), .a1(decoder48_1_a1), .b1(decoder48_1_b1),
    .c1(decoder48_1_c1), .d1(decoder48_1_d1), .e1(decoder48_1_e1), .f1(decoder48_1_f1), .g1(decoder48_1_g1));
  _7_Segment_Display u_7_segment_display_1 (
    .g(decoder48_1_g1), .f(decoder48_1_f1), .a(decoder48_1_a1), .b(decoder48_1_b1), .e(decoder48_1_e1),
    .d(decoder48_1_d1), .c(decoder48_1_c1));  // open: dp
endmodule
