// Logisim project sign_magnitude.circ as structural Verilog: 3 circuits, main circuit rca
module rca (
  input  [3:0] in_1,
  input  [3:0] in_2,
  output [3:0] out_3
);

  wire and_1_out, full_suber_4bit_input_1_bout, full_suber_4bit_input_2_bout, xor_1_out;
  wire [3:0] full_adder_4bit_input_1_s, full_suber_4bit_input_1_d, full_suber_4bit_input_2_d,
       multiplexer_1_out, multiplexer_2_out, multiplexer_3_out, or_1_out, or_2_out;

  and and_1 (and_1_out, in_1[3], in_2[3]);
  full_adder_4bit_input full_adder_4bit_input_1 (.a(in_1), .b(in_2), .s(full_adder_4bit_input_1_s));  // open: cout
  assign or_1_out = full_adder_4bit_input_1_s | 4'b1000;  // OR_Gate or_1, 4 bits wide
  xor xor_1 (xor_1_out, in_1[3], in_2[3]);
  Multiplexer #(.width(4)) multiplexer_1 (
    .in0(full_adder_4bit_input_1_s), .in1(or_1_out), .out(multiplexer_1_out), .sel(and_1_out));
  full_suber_4bit_input full_suber_4bit_input_1 (
    .a({1'b0, in_1[2:0]}), .b({1'b0, in_2[2:0]}), .d(full_suber_4bit_input_1_d),
    .bout(full_suber_4bit_input_1_bout));
  full_suber_4bit_input full_suber_4bit_input_2 (
    .a({1'b0, in_2[2:0]}), .b({1'b0, in_1[2:0]}), .d(full_suber_4bit_input_2_d),
    .bout(full_suber_4bit_input_2_bout));
  Multiplexer #(.width(4)) multiplexer_2 (
    .in0(full_suber_4bit_input_1_d), .in1(full_suber_4bit_input_2_d), .out(multiplexer_2_out),
    .sel(full_suber_4bit_input_1_bout));
  Multiplexer #(.width(4)) multiplexer_3 (
    .in0({in_1[3], 3'b000}), .in1({in_2[3], 3'b000}), .out(multiplexer_3_out),
    .sel(full_suber_4bit_input_1_bout));
  assign or_2_out = multiplexer_2_out | multiplexer_3_out;  // OR_Gate or_2, 4 bits wide
  Multiplexer #(.width(4)) multiplexer_4 (.in0(multiplexer_1_out), .in1(or_2_out), .out(out_3), .sel(xor_1_out));
endmodule

module test_rca (
);

  wire [2:0] rca_1_out_3_2;
  wire [3:0] dipswitch_1_sw4, dipswitch_2_sw4;
  wire [3:3] rca_1_out_3;

  DipSwitch #(.number(4)) dipswitch_1 (
    .sw1(dipswitch_1_sw4[3]), .sw2(dipswitch_1_sw4[2]), .sw3(dipswitch_1_sw4[1]), .sw4(dipswitch_1_sw4[0]));
  DipSwitch #(.number(4)) dipswitch_2 (
    .sw1(dipswitch_2_sw4[3]), .sw2(dipswitch_2_sw4[2]), .sw3(dipswitch_2_sw4[1]), .sw4(dipswitch_2_sw4[0]));
  rca rca_1 (.in_1(dipswitch_1_sw4), .in_2(dipswitch_2_sw4), .out_3({rca_1_out_3[3], rca_1_out_3_2}));
  _7_Segment_Display u_7_segment_display_1 (.g(rca_1_out_3[3]));  // open: f, a, b, e, d, c, dp
  Hex_Digit_Display hex_digit_display_1 (.value({1'b0, rca_1_out_3_2}));  // open: dp
endmodule

module one_complement (
);

  wire [3:0] dipswitch_1_sw4, dipswitch_2_sw4, multiplexer_1_out, multiplexer_2_out, multiplexer_3_out,
       not_1_out, not_2_out, not_3_out, or_1_out, or_2_out, rca_1_out_3;

  DipSwitch #(.number(4)) dipswitch_1 (
    .sw1(dipswitch_1_sw4[3]), .sw2(dipswitch_1_sw4[2]), .sw3(dipswitch_1_sw4[1]), .sw4(dipswitch_1_sw4[0]));
  DipSwitch #(.number(4)) dipswitch_2 (
    .sw1(dipswitch_2_sw4[3]), .sw2(dipswitch_2_sw4[2]), .sw3(dipswitch_2_sw4[1]), .sw4(dipswitch_2_sw4[0]));
  assign not_1_out = ~dipswitch_1_sw4;  // NOT_Gate not_1, 4 bits wide
  assign not_2_out = ~dipswitch_2_sw4;  // NOT_Gate not_2, 4 bits wide
  assign or_1_out = not_1_out | {dipswitch_1_sw4[3], 3'b000};  // OR_Gate or_1, 4 bits wide
  assign or_2_out = not_2_out | {dipswitch_2_sw4[3], 3'b000};  // OR_Gate or_2, 4 bits wide
  Multiplexer #(.width(4)) multiplexer_1 (
    .in0(dipswitch_1_sw4), .in1(or_1_out), .out(multiplexer_1_out), .sel(dipswitch_1_sw4[3]));
  Multiplexer #(.width(4)) multiplexer_2 (
    .in0(dipswitch_2_sw4), .in1(or_2_out), .out(multiplexer_2_out), .sel(dipswitch_2_sw4[3]));
  rca rca_1 (.in_1(multiplexer_1_out), .in_2(multiplexer_2_out), .out_3(rca_1_out_3));
  assign not_3_out = ~{1'b0, rca_1_out_3[2:0]};  // NOT_Gate not_3, 4 bits wide
  Multiplexer #(.width(4)) multiplexer_3 (
    .in0(rca_1_out_3), .in1(not_3_out), .out(multiplexer_3_out), .sel(rca_1_out_3[3]));
  Hex_Digit_Display hex_digit_display_1 (.value(multiplexer_3_out));  // open: dp
endmodule
